// Logisim project Conterexamples.circ as structural Verilog: 7 circuits, main circuit NOT Gate
module NOT_Gate (
  input  in_1,
  output out_2
);

  Pull_Resistor #(.pull(1)) pull_resistor_1 (.node(out_2));
  Transistor #(.\type ("n")) transistor_1 (.in(1'b0), .out(out_2), .gate(in_1));
endmodule

module XOR1 (
  input  in_1,
  input  in_2,
  output out_3
);

  wire and_1_out, and_2_out, not_1_out, not_2_out;

  not not_1 (not_1_out, in_2);
  not not_2 (not_2_out, in_1);
  and and_1 (and_1_out, in_1, not_1_out);
  or or_1 (out_3, and_1_out, and_2_out);
  and and_2 (and_2_out, not_2_out, in_2);
endmodule

module XOR2 (
  input  in_1,
  input  in_2,
  output out_3
);

  wire nand_1_out, or_1_out;

  or or_1 (or_1_out, in_1, in_2);
  nand nand_1 (nand_1_out, in_1, in_2);
  and and_1 (out_3, or_1_out, nand_1_out);
endmodule

module XOR3 (
  input  in_1,
  input  in_2,
  output out_3
);

  wire nand_1_out, nand_2_out, nand_3_out, nand_4_out, nand_5_out, nand_6_out, nand_7_out, nand_8_out,
       nand_9_out;

  nand nand_1 (nand_1_out, in_1, in_1);
  nand nand_2 (nand_2_out, in_2, in_2);
  nand nand_3 (nand_3_out, in_1, in_1);
  nand nand_4 (nand_4_out, in_2, in_2);
  nand nand_5 (nand_5_out, nand_1_out, nand_2_out);
  nand nand_6 (nand_6_out, in_1, in_2);
  nand nand_7 (nand_7_out, nand_3_out, nand_4_out);
  nand nand_8 (nand_8_out, nand_5_out, nand_6_out);
  nand nand_9 (nand_9_out, nand_6_out, nand_7_out);
  nand nand_10 (out_3, nand_8_out, nand_9_out);
endmodule

module XOR4 (
  input  a,
  input  b,
  output x
);

  wire nand_1_out, nand_2_out, nand_3_out, nand_4_out, nand_5_out;

  nand nand_1 (nand_1_out, a, a);
  nand nand_2 (nand_2_out, b, b);
  nand nand_3 (nand_3_out, nand_1_out, nand_2_out);
  nand nand_4 (nand_4_out, a, b);
  nand nand_5 (nand_5_out, nand_3_out, nand_4_out);
  nand nand_6 (x, nand_5_out, nand_5_out);
endmodule

module XOR5 (
  input  in_1,
  input  in_2,
  output out_3
);

  wire nand_1_out, nand_2_out, nand_3_out;

  nand nand_1 (nand_1_out, in_1, nand_2_out);
  nand nand_2 (nand_2_out, in_1, in_2);
  nand nand_3 (nand_3_out, nand_2_out, in_2);
  nand nand_4 (out_3, nand_1_out, nand_3_out);
endmodule

module XOR6 (
  input  in_1,
  input  in_2,
  output out_3
);

  wire transistor_1_out, transistor_2_out, transistor_5_out, transistor_7_out, transistor_9_out,
       transistor_12_out, transistor_15_out;

  Transistor transistor_1 (.in(1'b1), .out(transistor_1_out), .gate(in_1));
  Transistor transistor_2 (.in(1'b1), .out(transistor_2_out), .gate(transistor_1_out));
  Transistor transistor_3 (.in(1'b1), .out(transistor_1_out), .gate(in_2));
  Transistor #(.\type ("n")) transistor_4 (.in(transistor_5_out), .out(transistor_1_out), .gate(in_1));
  Transistor #(.\type ("n")) transistor_5 (.in(1'b0), .out(transistor_5_out), .gate(in_2));
  Transistor #(.\type ("n")) transistor_6 (.in(transistor_7_out), .out(transistor_2_out), .gate(transistor_1_out));
  Transistor #(.\type ("n")) transistor_7 (.in(1'b0), .out(transistor_7_out), .gate(in_2));
  Transistor transistor_8 (.in(1'b1), .out(transistor_2_out), .gate(in_2));
  Transistor transistor_9 (.in(1'b1), .out(transistor_9_out), .gate(in_1));
  Transistor transistor_10 (.in(1'b1), .out(transistor_9_out), .gate(transistor_1_out));
  Transistor #(.\type ("n")) transistor_11 (.in(transistor_12_out), .out(transistor_9_out), .gate(in_1));
  Transistor #(.\type ("n")) transistor_12 (.in(1'b0), .out(transistor_12_out), .gate(transistor_1_out));
  Transistor transistor_13 (.in(1'b1), .out(out_3), .gate(transistor_9_out));
  Transistor #(.\type ("n")) transistor_14 (.in(transistor_15_out), .out(out_3), .gate(transistor_9_out));
  Transistor #(.\type ("n")) transistor_15 (.in(1'b0), .out(transistor_15_out), .gate(transistor_2_out));
  Transistor transistor_16 (.in(1'b1), .out(out_3), .gate(transistor_2_out));
endmodule
