// Logisim project Progress.circ as structural Verilog: 6 circuits, main circuit computer adder
module computer_adder (
  input  \бит_переноса ,
  input  \а0 ,
  input  \а1 ,
  input  \а2 ,
  input  \б0 ,
  input  \б1 ,
  input  \б2 ,
  output \бит_переноса_2 ,
  output \в2 ,
  output \в1 ,
  output \в0 
);

  wire adder_1_cout, adder_2_cout;

  Adder #(.width(1)) adder_1 (.a(\а0 ), .b(\б0 ), .out(\в0 ), .cin(\бит_переноса ), .cout(adder_1_cout));
  Adder #(.width(1)) adder_2 (.a(\а1 ), .b(\б1 ), .out(\в1 ), .cin(adder_1_cout), .cout(adder_2_cout));
  Adder #(.width(1)) adder_3 (.a(\а2 ), .b(\б2 ), .out(\в2 ), .cin(adder_2_cout), .cout(\бит_переноса_2 ));
endmodule

module detailed_computer_adder (
  input  a,
  input  b,
  input  c,
  input  d,
  input  e,
  input  f,
  input  g,
  output x,
  output y,
  output z,
  output u
);

  wire and_1_out, and_2_out, and_3_out, and_4_out, and_5_out, and_6_out, and_7_out, and_8_out, and_9_out,
       and_10_out, and_11_out, and_12_out, and_13_out, and_14_out, and_15_out, and_16_out, and_17_out,
       and_18_out, and_19_out, and_20_out, and_21_out, and_22_out, and_23_out, and_24_out, and_25_out,
       and_26_out, and_27_out, and_28_out, and_29_out, and_30_out, and_31_out, and_32_out, and_33_out,
       and_34_out, and_35_out, and_36_out, and_37_out, and_38_out, and_39_out, and_40_out, and_41_out,
       and_42_out, and_43_out, and_44_out, and_45_out, and_46_out, and_47_out, and_48_out, and_49_out,
       and_50_out, and_51_out, and_52_out, and_53_out, and_54_out, and_55_out, and_56_out, and_57_out,
       and_58_out, and_59_out, and_60_out, and_61_out, and_62_out, and_63_out, and_64_out, and_65_out,
       and_66_out, and_67_out, and_68_out, and_69_out, and_70_out, and_71_out, and_72_out, and_73_out,
       and_74_out, and_75_out, and_76_out, and_77_out, and_78_out, and_79_out, and_80_out, and_81_out,
       and_82_out, and_83_out, and_84_out, and_85_out, and_86_out, and_87_out, and_88_out, and_89_out,
       and_90_out, and_91_out, and_92_out, and_93_out, and_94_out, and_95_out, and_96_out, and_97_out,
       and_98_out, and_99_out, and_100_out, and_101_out, and_102_out, and_103_out, and_104_out, and_105_out,
       and_106_out, and_107_out, and_108_out, and_109_out, and_110_out, and_111_out, and_112_out,
       and_113_out, and_114_out, and_115_out, and_116_out, and_117_out, and_118_out, and_119_out,
       and_120_out, and_121_out, and_122_out, and_123_out, and_124_out, and_125_out, and_126_out,
       and_127_out, and_128_out, and_129_out, and_130_out, and_131_out, and_132_out, and_133_out,
       and_134_out, and_135_out, and_136_out, and_137_out, and_138_out, and_139_out, and_140_out,
       and_141_out, and_142_out, and_143_out, and_144_out, and_145_out, and_146_out, and_147_out,
       and_148_out, and_149_out, and_150_out, and_151_out, and_152_out, and_153_out, and_154_out,
       and_155_out, and_156_out, and_157_out, and_158_out, and_159_out, and_160_out, and_161_out,
       and_162_out, and_163_out, and_164_out, and_165_out, not_1_out, not_2_out, not_3_out, not_4_out,
       not_5_out, not_6_out, not_7_out, not_8_out, not_9_out, not_10_out, not_11_out, not_12_out, not_13_out,
       not_14_out, not_15_out, not_16_out, not_17_out, not_18_out, not_19_out, not_20_out, not_21_out,
       not_22_out, not_23_out, not_24_out, not_25_out, not_26_out, not_27_out, not_28_out, not_29_out,
       not_30_out, not_31_out, not_32_out, not_33_out, not_34_out, not_35_out, not_36_out, not_37_out,
       not_38_out, not_39_out, not_40_out, not_41_out, not_42_out, not_43_out, not_44_out, not_45_out,
       not_46_out, not_47_out, not_48_out, not_49_out, not_50_out, not_51_out, not_52_out, not_53_out,
       not_54_out, not_55_out, not_56_out, not_57_out, not_58_out, not_59_out, not_60_out, not_61_out,
       not_62_out, not_63_out, not_64_out, not_65_out, not_66_out, not_67_out, not_68_out, not_69_out,
       not_70_out, not_71_out, not_72_out, not_73_out, not_74_out, not_75_out, not_76_out, not_77_out,
       not_78_out, not_79_out, not_80_out, not_81_out, not_82_out, not_83_out, not_84_out, not_85_out,
       not_86_out, not_87_out, not_88_out, not_89_out, not_90_out, not_91_out, not_92_out, not_93_out,
       not_94_out, not_95_out, not_96_out, not_97_out, not_98_out, or_1_out, or_2_out, or_3_out, or_4_out,
       or_5_out, or_6_out, or_7_out, or_8_out, or_9_out, or_10_out, or_11_out, or_12_out, or_13_out,
       or_14_out, or_15_out, or_16_out, or_17_out, or_18_out, or_19_out, or_20_out, or_21_out, or_22_out,
       or_23_out, or_24_out, or_25_out, or_26_out, or_27_out, or_28_out, or_29_out, or_30_out, or_31_out,
       or_32_out, or_33_out, or_34_out, or_35_out, or_36_out, or_37_out, or_38_out, or_39_out, or_40_out,
       or_41_out, or_42_out, or_43_out, or_44_out, or_45_out, or_46_out, or_47_out, or_48_out, or_49_out,
       or_50_out, or_51_out, or_52_out, or_53_out, or_54_out, or_55_out, or_56_out, or_57_out, or_58_out,
       or_59_out, or_60_out, or_61_out, or_62_out, or_63_out, or_65_out, or_66_out, or_67_out, or_68_out,
       or_69_out, or_70_out, or_71_out, or_72_out, or_73_out, or_74_out, or_75_out, or_76_out, or_77_out,
       or_78_out, or_79_out, or_80_out;

  or or_1 (or_1_out, a, b);
  or or_2 (or_2_out, c, d);
  or or_3 (or_3_out, a, b);
  or or_4 (or_4_out, c, g);
  or or_5 (or_5_out, a, b);
  or or_6 (or_6_out, d, f);
  or or_7 (or_7_out, a, b);
  or or_8 (or_8_out, f, g);
  or or_9 (or_9_out, a, c);
  or or_10 (or_10_out, d, e);
  or or_11 (or_11_out, a, c);
  or or_12 (or_12_out, e, g);
  or or_13 (or_13_out, a, d);
  or or_14 (or_14_out, e, f);
  or or_15 (or_15_out, a, e);
  or or_16 (or_16_out, f, g);
  or or_17 (or_17_out, b, c);
  or or_18 (or_18_out, d, e);
  or or_19 (or_19_out, b, c);
  or or_20 (or_20_out, e, g);
  or or_21 (or_21_out, b, d);
  or or_22 (or_22_out, e, f);
  or or_23 (or_23_out, b, e);
  or or_24 (or_24_out, f, g);
  or or_25 (or_25_out, c, d);
  or or_26 (or_26_out, c, f);
  not not_1 (not_1_out, a);
  not not_2 (not_2_out, b);
  not not_3 (not_3_out, a);
  not not_4 (not_4_out, b);
  not not_5 (not_5_out, a);
  not not_6 (not_6_out, c);
  not not_7 (not_7_out, a);
  not not_8 (not_8_out, d);
  not not_9 (not_9_out, b);
  not not_10 (not_10_out, c);
  not not_11 (not_11_out, b);
  not not_12 (not_12_out, d);
  not not_13 (not_13_out, a);
  not not_14 (not_14_out, b);
  not not_15 (not_15_out, a);
  not not_16 (not_16_out, b);
  not not_17 (not_17_out, a);
  not not_18 (not_18_out, c);
  not not_19 (not_19_out, a);
  not not_20 (not_20_out, b);
  not not_21 (not_21_out, c);
  not not_22 (not_22_out, b);
  not not_23 (not_23_out, d);
  not not_24 (not_24_out, a);
  not not_25 (not_25_out, b);
  not not_26 (not_26_out, c);
  not not_27 (not_27_out, a);
  not not_28 (not_28_out, c);
  not not_29 (not_29_out, e);
  not not_30 (not_30_out, a);
  not not_31 (not_31_out, b);
  not not_32 (not_32_out, f);
  not not_33 (not_33_out, a);
  not not_34 (not_34_out, e);
  not not_35 (not_35_out, f);
  not not_36 (not_36_out, c);
  not not_37 (not_37_out, f);
  not not_38 (not_38_out, c);
  not not_39 (not_39_out, f);
  not not_40 (not_40_out, a);
  not not_41 (not_41_out, b);
  not not_42 (not_42_out, a);
  not not_43 (not_43_out, b);
  or or_27 (or_27_out, or_1_out, or_2_out);
  or or_28 (or_28_out, or_3_out, or_4_out);
  or or_29 (or_29_out, or_5_out, or_6_out);
  or or_30 (or_30_out, or_7_out, or_8_out);
  or or_31 (or_31_out, or_9_out, or_10_out);
  or or_32 (or_32_out, or_11_out, or_12_out);
  or or_33 (or_33_out, or_13_out, or_14_out);
  or or_34 (or_34_out, or_15_out, or_16_out);
  or or_35 (or_35_out, or_17_out, or_18_out);
  or or_36 (or_36_out, or_19_out, or_20_out);
  or or_37 (or_37_out, or_21_out, or_22_out);
  or or_38 (or_38_out, or_23_out, or_24_out);
  or or_39 (or_39_out, or_25_out, f);
  or or_40 (or_40_out, or_26_out, g);
  and and_1 (and_1_out, not_1_out, not_2_out);
  not not_44 (not_44_out, c);
  not not_45 (not_45_out, d);
  and and_2 (and_2_out, not_3_out, not_4_out);
  not not_46 (not_46_out, d);
  not not_47 (not_47_out, f);
  and and_3 (and_3_out, not_5_out, not_6_out);
  not not_48 (not_48_out, d);
  not not_49 (not_49_out, e);
  and and_4 (and_4_out, not_7_out, not_8_out);
  not not_50 (not_50_out, e);
  not not_51 (not_51_out, f);
  and and_5 (and_5_out, not_9_out, not_10_out);
  not not_52 (not_52_out, d);
  not not_53 (not_53_out, e);
  and and_6 (and_6_out, not_11_out, not_12_out);
  not not_54 (not_54_out, e);
  not not_55 (not_55_out, f);
  and and_7 (and_7_out, not_13_out, not_14_out);
  not not_56 (not_56_out, c);
  not not_57 (not_57_out, g);
  and and_8 (and_8_out, not_15_out, not_16_out);
  not not_58 (not_58_out, f);
  not not_59 (not_59_out, g);
  and and_9 (and_9_out, not_17_out, not_18_out);
  not not_60 (not_60_out, e);
  not not_61 (not_61_out, g);
  and and_10 (and_10_out, not_19_out, d);
  not not_62 (not_62_out, e);
  not not_63 (not_63_out, f);
  not not_64 (not_64_out, g);
  and and_11 (and_11_out, not_20_out, not_21_out);
  not not_65 (not_65_out, e);
  not not_66 (not_66_out, g);
  and and_12 (and_12_out, not_22_out, d);
  not not_67 (not_67_out, e);
  not not_68 (not_68_out, f);
  not not_69 (not_69_out, g);
  not not_70 (not_70_out, d);
  not not_71 (not_71_out, g);
  and and_13 (and_13_out, b, not_23_out);
  not not_72 (not_72_out, g);
  and and_14 (and_14_out, b, d);
  and and_15 (and_15_out, b, c);
  not not_73 (not_73_out, d);
  not not_74 (not_74_out, g);
  and and_16 (and_16_out, b, c);
  not not_75 (not_75_out, d);
  and and_17 (and_17_out, a, d);
  and and_18 (and_18_out, a, c);
  not not_76 (not_76_out, d);
  not not_77 (not_77_out, g);
  and and_19 (and_19_out, a, c);
  and and_20 (and_20_out, a, b);
  not not_78 (not_78_out, d);
  not not_79 (not_79_out, g);
  and and_21 (and_21_out, a, b);
  and and_22 (and_22_out, a, b);
  not not_80 (not_80_out, d);
  not not_81 (not_81_out, g);
  and and_23 (and_23_out, not_24_out, not_25_out);
  and and_24 (and_24_out, not_26_out, f);
  and and_25 (and_25_out, not_27_out, not_28_out);
  and and_26 (and_26_out, not_29_out, f);
  not not_82 (not_82_out, b);
  not not_83 (not_83_out, c);
  not not_84 (not_84_out, e);
  and and_27 (and_27_out, not_30_out, not_31_out);
  and and_28 (and_28_out, c, not_32_out);
  and and_29 (and_29_out, not_33_out, c);
  and and_30 (and_30_out, not_34_out, not_35_out);
  not not_85 (not_85_out, b);
  not not_86 (not_86_out, e);
  not not_87 (not_87_out, f);
  and and_31 (and_31_out, b, not_36_out);
  and and_32 (and_32_out, e, not_37_out);
  and and_33 (and_33_out, b, c);
  and and_34 (and_34_out, e, f);
  not not_88 (not_88_out, c);
  not not_89 (not_89_out, f);
  and and_35 (and_35_out, a, c);
  and and_36 (and_36_out, e, f);
  and and_37 (and_37_out, a, b);
  and and_38 (and_38_out, not_38_out, not_39_out);
  and and_39 (and_39_out, not_40_out, not_41_out);
  and and_40 (and_40_out, not_42_out, b);
  not not_90 (not_90_out, e);
  and and_41 (and_41_out, a, not_43_out);
  not not_91 (not_91_out, e);
  and and_42 (and_42_out, a, b);
  and and_43 (and_43_out, or_27_out, or_28_out);
  and and_44 (and_44_out, or_29_out, or_30_out);
  and and_45 (and_45_out, or_31_out, or_32_out);
  and and_46 (and_46_out, or_33_out, or_34_out);
  and and_47 (and_47_out, or_35_out, or_36_out);
  and and_48 (and_48_out, or_37_out, or_38_out);
  and and_49 (and_49_out, or_39_out, or_40_out);
  or or_41 (or_41_out, d, g);
  and and_50 (and_50_out, and_1_out, not_44_out);
  and and_51 (and_51_out, not_45_out, g);
  and and_52 (and_52_out, and_2_out, not_46_out);
  and and_53 (and_53_out, not_47_out, g);
  and and_54 (and_54_out, and_3_out, not_48_out);
  and and_55 (and_55_out, not_49_out, g);
  and and_56 (and_56_out, and_4_out, not_50_out);
  and and_57 (and_57_out, not_51_out, g);
  and and_58 (and_58_out, and_5_out, not_52_out);
  and and_59 (and_59_out, not_53_out, g);
  and and_60 (and_60_out, and_6_out, not_54_out);
  and and_61 (and_61_out, not_55_out, g);
  not not_92 (not_92_out, c);
  not not_93 (not_93_out, d);
  not not_94 (not_94_out, f);
  and and_62 (and_62_out, and_7_out, not_56_out);
  and and_63 (and_63_out, d, not_57_out);
  and and_64 (and_64_out, and_8_out, d);
  and and_65 (and_65_out, not_58_out, not_59_out);
  and and_66 (and_66_out, and_9_out, d);
  and and_67 (and_67_out, not_60_out, not_61_out);
  and and_68 (and_68_out, and_10_out, not_62_out);
  and and_69 (and_69_out, not_63_out, not_64_out);
  and and_70 (and_70_out, and_11_out, d);
  and and_71 (and_71_out, not_65_out, not_66_out);
  and and_72 (and_72_out, and_12_out, not_67_out);
  and and_73 (and_73_out, not_68_out, not_69_out);
  not not_95 (not_95_out, c);
  not not_96 (not_96_out, f);
  not not_97 (not_97_out, g);
  and and_74 (and_74_out, c, not_70_out);
  and and_75 (and_75_out, f, not_71_out);
  and and_76 (and_76_out, c, d);
  and and_77 (and_77_out, f, g);
  and and_78 (and_78_out, and_13_out, e);
  and and_79 (and_79_out, f, not_72_out);
  and and_80 (and_80_out, and_14_out, e);
  and and_81 (and_81_out, f, g);
  and and_82 (and_82_out, and_15_out, not_73_out);
  and and_83 (and_83_out, e, not_74_out);
  and and_84 (and_84_out, and_16_out, d);
  and and_85 (and_85_out, e, g);
  and and_86 (and_86_out, a, not_75_out);
  not not_98 (not_98_out, g);
  and and_87 (and_87_out, and_17_out, e);
  and and_88 (and_88_out, f, g);
  and and_89 (and_89_out, and_18_out, not_76_out);
  and and_90 (and_90_out, e, not_77_out);
  and and_91 (and_91_out, and_19_out, d);
  and and_92 (and_92_out, e, g);
  and and_93 (and_93_out, and_20_out, not_78_out);
  and and_94 (and_94_out, f, not_79_out);
  and and_95 (and_95_out, and_21_out, d);
  and and_96 (and_96_out, f, g);
  and and_97 (and_97_out, and_22_out, c);
  and and_98 (and_98_out, not_80_out, not_81_out);
  and and_99 (and_99_out, a, b);
  and and_100 (and_100_out, and_23_out, and_24_out);
  and and_101 (and_101_out, and_25_out, and_26_out);
  and and_102 (and_102_out, not_82_out, not_83_out);
  and and_103 (and_103_out, not_84_out, f);
  and and_104 (and_104_out, and_27_out, and_28_out);
  and and_105 (and_105_out, and_29_out, and_30_out);
  and and_106 (and_106_out, not_85_out, c);
  and and_107 (and_107_out, not_86_out, not_87_out);
  and and_108 (and_108_out, and_31_out, and_32_out);
  and and_109 (and_109_out, and_33_out, and_34_out);
  and and_110 (and_110_out, a, not_88_out);
  and and_111 (and_111_out, e, not_89_out);
  and and_112 (and_112_out, and_35_out, and_36_out);
  and and_113 (and_113_out, and_37_out, and_38_out);
  and and_114 (and_114_out, a, b);
  and and_115 (and_115_out, c, f);
  and and_116 (and_116_out, and_39_out, e);
  and and_117 (and_117_out, and_40_out, not_90_out);
  and and_118 (and_118_out, and_41_out, not_91_out);
  and and_119 (and_119_out, and_42_out, e);
  and and_120 (and_120_out, and_43_out, and_44_out);
  and and_121 (and_121_out, and_45_out, and_46_out);
  and and_122 (and_122_out, and_47_out, and_48_out);
  and and_123 (and_123_out, and_49_out, or_41_out);
  and and_124 (and_124_out, and_50_out, and_51_out);
  and and_125 (and_125_out, and_52_out, and_53_out);
  and and_126 (and_126_out, and_54_out, and_55_out);
  and and_127 (and_127_out, and_56_out, and_57_out);
  and and_128 (and_128_out, and_58_out, and_59_out);
  and and_129 (and_129_out, and_60_out, and_61_out);
  and and_130 (and_130_out, not_92_out, not_93_out);
  and and_131 (and_131_out, not_94_out, g);
  and and_132 (and_132_out, and_62_out, and_63_out);
  and and_133 (and_133_out, and_64_out, and_65_out);
  and and_134 (and_134_out, and_66_out, and_67_out);
  and and_135 (and_135_out, and_68_out, and_69_out);
  and and_136 (and_136_out, and_70_out, and_71_out);
  and and_137 (and_137_out, and_72_out, and_73_out);
  and and_138 (and_138_out, not_95_out, d);
  and and_139 (and_139_out, not_96_out, not_97_out);
  and and_140 (and_140_out, and_74_out, and_75_out);
  and and_141 (and_141_out, and_76_out, and_77_out);
  and and_142 (and_142_out, and_78_out, and_79_out);
  and and_143 (and_143_out, and_80_out, and_81_out);
  and and_144 (and_144_out, and_82_out, and_83_out);
  and and_145 (and_145_out, and_84_out, and_85_out);
  and and_146 (and_146_out, and_86_out, e);
  and and_147 (and_147_out, f, not_98_out);
  and and_148 (and_148_out, and_87_out, and_88_out);
  and and_149 (and_149_out, and_89_out, and_90_out);
  and and_150 (and_150_out, and_91_out, and_92_out);
  and and_151 (and_151_out, and_93_out, and_94_out);
  and and_152 (and_152_out, and_95_out, and_96_out);
  and and_153 (and_153_out, and_97_out, and_98_out);
  and and_154 (and_154_out, and_99_out, c);
  and and_155 (and_155_out, d, g);
  or or_42 (or_42_out, and_100_out, and_101_out);
  and and_156 (and_156_out, and_102_out, and_103_out);
  or or_43 (or_43_out, and_104_out, and_105_out);
  and and_157 (and_157_out, and_106_out, and_107_out);
  or or_44 (or_44_out, and_108_out, and_109_out);
  and and_158 (and_158_out, and_110_out, and_111_out);
  or or_45 (or_45_out, and_112_out, and_113_out);
  and and_159 (and_159_out, and_114_out, and_115_out);
  or or_46 (or_46_out, and_116_out, and_117_out);
  or or_47 (or_47_out, and_118_out, and_119_out);
  and and_160 (and_160_out, and_120_out, and_121_out);
  and and_161 (and_161_out, and_122_out, and_123_out);
  or or_48 (or_48_out, and_124_out, and_125_out);
  or or_49 (or_49_out, and_126_out, and_127_out);
  or or_50 (or_50_out, and_128_out, and_129_out);
  and and_162 (and_162_out, and_130_out, and_131_out);
  or or_51 (or_51_out, and_132_out, and_133_out);
  or or_52 (or_52_out, and_134_out, and_135_out);
  or or_53 (or_53_out, and_136_out, and_137_out);
  and and_163 (and_163_out, and_138_out, and_139_out);
  or or_54 (or_54_out, and_140_out, and_141_out);
  or or_55 (or_55_out, and_142_out, and_143_out);
  or or_56 (or_56_out, and_144_out, and_145_out);
  and and_164 (and_164_out, and_146_out, and_147_out);
  or or_57 (or_57_out, and_148_out, and_149_out);
  or or_58 (or_58_out, and_150_out, and_151_out);
  or or_59 (or_59_out, and_152_out, and_153_out);
  and and_165 (and_165_out, and_154_out, and_155_out);
  or or_60 (or_60_out, or_42_out, and_156_out);
  or or_61 (or_61_out, or_43_out, and_157_out);
  or or_62 (or_62_out, or_44_out, and_158_out);
  or or_63 (or_63_out, or_45_out, and_159_out);
  or or_64 (u, or_46_out, or_47_out);
  and and_166 (x, and_160_out, and_161_out);
  or or_65 (or_65_out, or_48_out, or_49_out);
  or or_66 (or_66_out, or_50_out, and_162_out);
  or or_67 (or_67_out, or_51_out, or_52_out);
  or or_68 (or_68_out, or_53_out, and_163_out);
  or or_69 (or_69_out, or_54_out, or_55_out);
  or or_70 (or_70_out, or_56_out, and_164_out);
  or or_71 (or_71_out, or_57_out, or_58_out);
  or or_72 (or_72_out, or_59_out, and_165_out);
  or or_73 (or_73_out, or_60_out, or_61_out);
  or or_74 (or_74_out, or_62_out, or_63_out);
  or or_75 (or_75_out, or_65_out, or_66_out);
  or or_76 (or_76_out, or_75_out, or_77_out);
  or or_77 (or_77_out, or_67_out, or_68_out);
  or or_78 (or_78_out, or_69_out, or_70_out);
  or or_79 (or_79_out, or_78_out, or_80_out);
  or or_80 (or_80_out, or_71_out, or_72_out);
  or or_81 (z, or_73_out, or_74_out);
  or or_82 (y, or_76_out, or_79_out);
endmodule

module semi_adder (
  input  in_1,
  input  in_2,
  output out_3,
  output out_4
);

  xor xor_1 (out_3, in_1, in_2);
  and and_1 (out_4, in_2, in_1);
endmodule

module adder (
  input  in_1,
  input  in_2,
  input  in_3,
  output out_4,
  output out_5
);

  wire semi_adder_1_out_3, semi_adder_1_out_4, semi_adder_2_out_4;

  semi_adder semi_adder_1 (.in_1(in_1), .in_2(in_2), .out_3(semi_adder_1_out_3), .out_4(semi_adder_1_out_4));
  semi_adder semi_adder_2 (.in_1(in_3), .in_2(semi_adder_1_out_3), .out_3(out_4), .out_4(semi_adder_2_out_4));
  or or_1 (out_5, semi_adder_2_out_4, semi_adder_1_out_4);
endmodule

module _3_bit_adder (
  input  \бит_переноса ,
  input  \а0 ,
  input  \а1 ,
  input  \а2 ,
  input  \б0 ,
  input  \б1 ,
  input  \б2 ,
  output \бит_переноса_2 ,
  output \в2 ,
  output \в1 ,
  output \в0 
);

  wire adder_1_out_5, adder_2_out_5;

  adder adder_1 (.in_1(\бит_переноса ), .in_2(\а0 ), .in_3(\б0 ), .out_4(\в0 ), .out_5(adder_1_out_5));
  adder adder_2 (.in_1(adder_1_out_5), .in_2(\а1 ), .in_3(\б1 ), .out_4(\в1 ), .out_5(adder_2_out_5));
  adder adder_3 (.in_1(adder_2_out_5), .in_2(\а2 ), .in_3(\б2 ), .out_4(\в2 ), .out_5(\бит_переноса_2 ));
endmodule

module _3_bit_adder1 (
  input  in_1,
  input  \а0 ,
  input  \б0 ,
  input  \а1 ,
  input  \б1 ,
  input  \а2 ,
  input  \б2 ,
  output \бит_переноса ,
  output \в2 ,
  output \в1 ,
  output \в0 
);

  wire and_1_out, and_2_out, and_3_out, and_4_out, and_5_out, and_6_out, or_1_out, or_2_out, xor_1_out,
       xor_3_out, xor_5_out;

  and and_1 (and_1_out, \а0 , in_1);
  xor xor_1 (xor_1_out, in_1, \а0 );
  and and_2 (and_2_out, xor_1_out, \б0 );
  xor xor_2 (\в0 , \б0 , xor_1_out);
  or or_1 (or_1_out, and_2_out, and_1_out);
  and and_3 (and_3_out, \а1 , or_1_out);
  xor xor_3 (xor_3_out, or_1_out, \а1 );
  and and_4 (and_4_out, xor_3_out, \б1 );
  xor xor_4 (\в1 , \б1 , xor_3_out);
  or or_2 (or_2_out, and_4_out, and_3_out);
  and and_5 (and_5_out, \а2 , or_2_out);
  xor xor_5 (xor_5_out, or_2_out, \а2 );
  and and_6 (and_6_out, xor_5_out, \б2 );
  xor xor_6 (\в2 , \б2 , xor_5_out);
  or or_3 (\бит_переноса , and_6_out, and_5_out);
endmodule
