// Logisim project main.circ as structural Verilog: 1 circuit, main circuit main
module main (
  input  \бит_переноса ,
  input  \а0 ,
  input  \б0 ,
  input  \а1 ,
  input  \б1 ,
  input  \а2 ,
  input  \б2 ,
  output \бит_переноса_2 ,
  output \в2 ,
  output \в1 ,
  output \в0 
);

  wire and_1_out, and_2_out, and_3_out, and_4_out, and_5_out, and_6_out, or_1_out, or_2_out, xor_1_out,
       xor_3_out, xor_5_out;

  and and_1 (and_1_out, \а0 , \бит_переноса );
  xor xor_1 (xor_1_out, \бит_переноса , \а0 );
  and and_2 (and_2_out, xor_1_out, \б0 );
  xor xor_2 (\в0 , \б0 , xor_1_out);
  or or_1 (or_1_out, and_2_out, and_1_out);
  and and_3 (and_3_out, \а1 , or_1_out);
  xor xor_3 (xor_3_out, or_1_out, \а1 );
  and and_4 (and_4_out, xor_3_out, \б1 );
  xor xor_4 (\в1 , \б1 , xor_3_out);
  or or_2 (or_2_out, and_4_out, and_3_out);
  and and_5 (and_5_out, \а2 , or_2_out);
  xor xor_5 (xor_5_out, or_2_out, \а2 );
  and and_6 (and_6_out, xor_5_out, \б2 );
  xor xor_6 (\в2 , \б2 , xor_5_out);
  or or_3 (\бит_переноса_2 , and_6_out, and_5_out);

  // Notes on the sheet:
  //   Полный сумматор (Full Adder) двух 3-битных входов.
  //   Комиссаров Данил 
endmodule
